// Logisim project Simulation.circ as structural Verilog: 1 circuit, main circuit main
module main (
);

  wire button_1_out, CLK, counter_1_carry, n74181_2_p1, n74181_2_p4, n74181_2_p24, not_1_out, or_1_out,
       or_2_out, RST;
  wire [3:0] counter_3_q, FLAGS, n74181_2_p21;
  wire [4:0] register_1_q;
  wire [6:0] n74181_2_p2;
  wire [7:0] A_q, B_q, BUS8, counter_1_q, counter_2_q, MAR_H_q, MAR_L_q, SP_q;
  wire [15:0] C_q, MEMBUS16;
  wire [29:0] n74181_1_p11;
  wire [31:30] rom_1_data;

  assign MEMBUS16 = n74181_1_p11[12] ? {8'h1, SP_q} : 16'bz;  // Controlled_Buffer controlled_buffer_1
  assign MEMBUS16[15:8] = BUS8;  // Buffer buffer_1, 8 bits wide
  assign MEMBUS16[7:0] = BUS8;  // Buffer buffer_2, 8 bits wide
  assign MEMBUS16 = n74181_1_p11[20] ? C_q : 16'bz;  // Controlled_Buffer controlled_buffer_2
  assign MEMBUS16 = n74181_1_p11[23] ? {MAR_H_q, MAR_L_q} : 16'bz;  // Controlled_Buffer controlled_buffer_3
  assign BUS8 = n74181_1_p11[7] ? B_q : 8'bz;  // Controlled_Buffer controlled_buffer_4
  assign BUS8 = n74181_1_p11[9] ? A_q : 8'bz;  // Controlled_Buffer controlled_buffer_5
  assign BUS8 = n74181_1_p11[11] ? {n74181_2_p21[2], n74181_2_p2} : 8'bz;  // Controlled_Buffer controlled_buffer_6
  Counter SP (
    .load(n74181_1_p11[13]), .D(BUS8), .count(or_1_out), .Q(SP_q), .up(not_1_out), .clk(CLK), .clr(RST));  // open: carry
  Register D (.D(MEMBUS16[15:8]), .en(n74181_1_p11[19]), .clk(CLK), .Q(C_q[15:8]), .clr(RST));
  Register C (.D(MEMBUS16[7:0]), .en(n74181_1_p11[17]), .clk(CLK), .Q(C_q[7:0]), .clr(RST));
  Register MAR_H (.D(MEMBUS16[15:8]), .en(n74181_1_p11[24]), .clk(CLK), .Q(MAR_H_q), .clr(RST));
  Register MAR_L (.D(MEMBUS16[7:0]), .en(n74181_1_p11[24]), .clk(CLK), .Q(MAR_L_q), .clr(RST));
  Counter counter_1 (
    .load(n74181_1_p11[22]), .D(MEMBUS16[7:0]), .count(n74181_1_p11[27]), .Q(counter_1_q),
    .carry(counter_1_carry), .up(1'b1), .clk(CLK), .clr(RST));
  Register B (.D(BUS8), .en(n74181_1_p11[8]), .clk(CLK), .Q(B_q), .clr(RST));
  Register A (.D(BUS8), .en(n74181_1_p11[10]), .clk(CLK), .Q(A_q), .clr(RST));
  or or_1 (or_1_out, n74181_1_p11[14], n74181_1_p11[15]);
  not not_1 (not_1_out, n74181_1_p11[15]);
  assign BUS8 = n74181_1_p11[18] ? C_q[15:8] : 8'bz;  // Controlled_Buffer controlled_buffer_7
  assign BUS8 = n74181_1_p11[16] ? C_q[7:0] : 8'bz;  // Controlled_Buffer controlled_buffer_8
  Counter counter_2 (
    .load(n74181_1_p11[22]), .D(MEMBUS16[15:8]), .count(counter_1_carry), .Q(counter_2_q), .up(1'b1),
    .clk(CLK), .clr(RST));  // open: carry
  assign MEMBUS16 = n74181_1_p11[21] ? {counter_2_q, counter_1_q} : 16'bz;  // Controlled_Buffer controlled_buffer_9
  assign BUS8 = n74181_1_p11[28] ? counter_2_q : 8'bz;  // Controlled_Buffer controlled_buffer_10
  assign BUS8 = n74181_1_p11[29] ? counter_1_q : 8'bz;  // Controlled_Buffer controlled_buffer_11
  // _74181 74181_1: pin names not known; wires that end beside it: B_q[0], A_q[1], A_q[0], B_q[1], n74181_1_p11[3], A_q[2], n74181_1_p11[2], B_q[2], n74181_1_p11[1], A_q[3], n74181_1_p11[0], B_q[3], n74181_1_p11[5], n74181_1_p11[4]
  RAM #(.addrWidth(16), .asyncread("true"), .databus("bidir")) ram_1 (
    .addr({MAR_H_q, MAR_L_q}), .we(n74181_1_p11[26]), .oe(n74181_1_p11[25]), .clk(CLK));  // open: data
  // _74181 74181_2: pin names not known; wires that end beside it: n74181_2_p1, n74181_2_p2[0], n74181_2_p2[1], n74181_2_p4, n74181_2_p2[2], n74181_2_p2[3], B_q[4], A_q[5], A_q[4], B_q[5], n74181_1_p11[3], A_q[6], n74181_1_p11[2], B_q[6], n74181_1_p11[1], A_q[7], n74181_1_p11[0], B_q[7], n74181_2_p1, n74181_1_p11[4], n74181_2_p21[0], n74181_2_p2[4], n74181_2_p2[5], n74181_2_p24, n74181_2_p2[6], n74181_2_p21[2]
  Register #(.width(5)) register_1 (.D(BUS8[4:0]), .en(rom_1_data[30]), .clk(CLK), .Q(register_1_q), .clr(RST));
  Counter #(.max('hf), .width(4)) counter_3 (
    .load(1'b0), .count(1'b1), .Q(counter_3_q), .up(1'b1), .clk(CLK), .clr(or_2_out));  // open: D, carry
  and and_1 (n74181_2_p21[3], n74181_2_p4, n74181_2_p24);
  or or_2 (or_2_out, rom_1_data[31], RST);
  Register #(.width(4)) F (.D(n74181_2_p21), .en(n74181_1_p11[6]), .clk(CLK), .Q(FLAGS), .clr(RST));
  and and_2 (n74181_2_p21[1], ~n74181_2_p2[0], ~n74181_2_p2[1], ~n74181_2_p2[2], ~n74181_2_p2[3], ~n74181_2_p2[4], ~n74181_2_p2[5], ~n74181_2_p2[6], ~n74181_2_p21[2]);  // AND_Gate
  ROM #(.addrWidth(12), .dataWidth(32)) rom_1 (
    .addr({FLAGS[2:0], counter_3_q, register_1_q}), .data({rom_1_data, n74181_1_p11}));
  Clock clock_1 (.out(CLK));
  Button button_1 (.out(button_1_out));
  Button button_2 (.out(RST));

  // Notes on the sheet:
  //   contents of rom_1 (hex, n*v repeats v):
  //   32*1200000 32*4a000000 0 6*1200000 20200 20200 80200 1200000 8000000 8000000 8000000 1200000 4000
  //   c69 c46 c6c c50 c5b c56 c5e 1001000 4000 8*0 a000400 a080000 a000100 a080000 a080000 a080000 480
  //   80000000 80000000 a080000 8000000 8000000 8000000 a080000 1001000 7*80000000 4008200 1001000 8*0
  //   80000000 1200000 80000000 1200000 1200000 1200000 10100 80000000 80000000 1200000 80000000 80000000
  //   80000000 1200000 2024000 8*80000000 2000400 8*0 80000000 a020000 80000000 a020000 a020000 a020000
  //   80000000 80000000 80000000 2020000 80000000 80000000 80000000 a020000 1001000 9*80000000 8*0
  //   80000000 1100000 80000000 1100000 1100000 1100000 80000000 80000000 80000000 500000 80000000
  //   80000000 80000000 1001000 2080000 9*80000000 8*0 80000000 2000400 80000000 2000100 4000200 4000080
  //   7*80000000 14008000 500000 9*80000000 8*0 13*80000000 1001000 10*80000000 8*0 13*80000000 24008000
  //   10*80000000 8*0 13*80000000 500000 10*80000000 8*0 24*80000000 8*0 24*80000000 8*0 24*80000000 8*0
  //   24*80000000 8*0 24*80000000 7*0 32*1200000 32*4a000000 0 6*1200000 20200 20200 80200 1200000 8000000
  //   1200000 8000000 1200000 4000 c69 c46 c6c c50 c5b c56 c5e 1001000 4000 8*0 a000400 a080000 a000100
  //   a080000 a080000 a080000 480 80000000 80000000 a080000 8000000 a080000 8000000 a080000 1001000
  //   7*80000000 4008200 1001000 8*0 80000000 1200000 80000000 1200000 1200000 1200000 10100 80000000
  //   80000000 1200000 80000000 1200000 80000000 1200000 2024000 8*80000000 2000400 8*0 80000000 a020000
  //   80000000 a020000 a020000 a020000 80000000 80000000 80000000 2020000 80000000 2020000 80000000
  //   a020000 1001000 9*80000000 8*0 80000000 1100000 80000000 1100000 1100000 1100000 80000000 80000000
  //   80000000 500000 80000000 500000 80000000 1001000 2080000 9*80000000 8*0 80000000 2000400 80000000
  //   2000100 4000200 4000080 7*80000000 14008000 500000 9*80000000 8*0 13*80000000 1001000 10*80000000
  //   8*0 13*80000000 24008000 10*80000000 8*0 13*80000000 500000 10*80000000 8*0 24*80000000 8*0
  //   24*80000000 8*0 24*80000000 8*0 24*80000000 8*0 24*80000000 7*0 32*1200000 32*4a000000 0 6*1200000
  //   20200 20200 80200 1200000 1200000 8000000 8000000 1200000 4000 c69 c46 c6c c50 c5b c56 c5e 1001000
  //   4000 8*0 a000400 a080000 a000100 a080000 a080000 a080000 480 80000000 80000000 a080000 a080000
  //   8000000 8000000 a080000 1001000 7*80000000 4008200 1001000 8*0 80000000 1200000 80000000 1200000
  //   1200000 1200000 10100 80000000 80000000 1200000 1200000 80000000 80000000 1200000 2024000 8*80000000
  //   2000400 8*0 80000000 a020000 80000000 a020000 a020000 a020000 80000000 80000000 80000000 2020000
  //   2020000 80000000 80000000 a020000 1001000 9*80000000 8*0 80000000 1100000 80000000 1100000 1100000
  //   1100000 80000000 80000000 80000000 500000 500000 80000000 80000000 1001000 2080000 9*80000000 8*0
  //   80000000 2000400 80000000 2000100 4000200 4000080 7*80000000 14008000 500000 9*80000000 8*0
  //   13*80000000 1001000 10*80000000 8*0 13*80000000 24008000 10*80000000 8*0 13*80000000 500000
  //   10*80000000 8*0 24*80000000 8*0 24*80000000 8*0 24*80000000 8*0 24*80000000 8*0 24*80000000 7*0
  //   32*1200000 32*4a000000 0 6*1200000 20200 20200 80200 1200000 1200000 1200000 8000000 1200000 4000
  //   c69 c46 c6c c50 c5b c56 c5e 1001000 4000 8*0 a000400 a080000 a000100 a080000 a080000 a080000 480
  //   80000000 80000000 a080000 a080000 a080000 8000000 a080000 1001000 7*80000000 4008200 1001000 8*0
  //   80000000 1200000 80000000 1200000 1200000 1200000 10100 80000000 80000000 1200000 1200000 1200000
  //   80000000 1200000 2024000 8*80000000 2000400 8*0 80000000 a020000 80000000 a020000 a020000 a020000
  //   80000000 80000000 80000000 2020000 2020000 2020000 80000000 a020000 1001000 9*80000000 8*0 80000000
  //   1100000 80000000 1100000 1100000 1100000 80000000 80000000 80000000 500000 500000 500000 80000000
  //   1001000 2080000 9*80000000 8*0 80000000 2000400 80000000 2000100 4000200 4000080 7*80000000 14008000
  //   500000 9*80000000 8*0 13*80000000 1001000 10*80000000 8*0 13*80000000 24008000 10*80000000 8*0
  //   13*80000000 500000 10*80000000 8*0 24*80000000 8*0 24*80000000 8*0 24*80000000 8*0 24*80000000 8*0
  //   24*80000000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
endmodule
